# Fritzing sketch powerboard (saved by Fritzing 0.9.0b)
stripboards: 1

parts:
  PRN_-_DATA = male pin header, 3 pins [form="♂ (male)"]
  BTN = Screw terminal - 2 pins [package=THT]
  R1 = Resistor [tolerance=±5% resistance=10k package=THT]
  BTN_-_ARDUINO = female pin header, 1 pin [form="♀ (female)"]
  C1 = Electrolytic Capacitor [capacitance=1000µF voltage=35V package="200 mil [THT, electrolytic]"]
  Power = Power Jack [package=power_jack_pth]
  D2 = Rectifier Diode [part_number=1N4001 package="300 mil [THT]"]
  LED_ARDUINO = female pin header, 1 pin [form="♀ (female)"]
  LED_-_PWR = female pin header, 3 pins [form="♀ (female)"]
  R2 = Resistor [tolerance=±5% resistance=330 package=THT]
  USB_-_PWR = female pin header, 3 pins [form="♀ (female)"]
  PRN_-_DATA_2 = female pin header, 3 pins [form="♀ (female)"]
  PRN_-_PWR = male pin header, 2 pins [form="♂ (male)"]

nets:
  N1: PRN_-_DATA.pin1, BTN.pin1, C1.-, Power.GND, LED_-_PWR.pin2, USB_-_PWR.pin1, USB_-_PWR.pin2, PRN_-_DATA_2.pin1, PRN_-_PWR.pin1
  N2: PRN_-_DATA.pin2, PRN_-_DATA_2.pin2
  N3: PRN_-_DATA.pin3, PRN_-_DATA_2.pin3
  N4: BTN.pin2, R1.Pin_1, BTN_-_ARDUINO.pin1
  N5: R1.Pin_0, Power.PWR, D2.anode, USB_-_PWR.pin3, PRN_-_PWR.pin2
  N6: C1.+, D2.cathode, LED_-_PWR.pin3
  N7: LED_ARDUINO.pin1, R2.Pin_0
  N8: LED_-_PWR.pin1, R2.Pin_1
